# Fritzing sketch design_perf_board (saved by Fritzing 0.9.3b)

parts:
  F1 = FUSE [package=fuse_5mm]
  F2 = FUSE [package=fuse_5mm]
  Part2 = Logic Level Converter
  J1 = female pin header, 6 pins [form="♀ (female)"]
  J2 = female pin header, 6 pins [form="♀ (female)"]
  J3 = female pin header, 6 pins [form="♀ (female)"]
  J5 = female pin header, 4 pins [form="♀ (female)"]
  J6 = female pin header, 4 pins [form="♀ (female)"]
  J8 = female pin header, 2 pins [form="♀ (female)"]
  LED1 = LED - 5mm [color="Red (633nm)" package="5 mm [THT]"]  # not connected
  LED2 = LED - 5mm [color="Green (570nm)" package="5 mm [THT]"]  # not connected
  Part3 = Arduino Due (Rev2b)  # not connected
  Part4 = Arduino ProtoShield  # not connected
  J7 = female pin header, 4 pins [form="♀ (female)"]
  Part5 = Arduino ProtoShield
  F3 = FUSE [package=fuse_5mm]
  F4 = FUSE [package=fuse_5mm]
  Part6 = Logic Level Converter
  J9 = female pin header, 2 pins [form="♀ (female)"]
  J12 = female pin header, 4 pins [form="♀ (female)"]
  J13 = female pin header, 4 pins [form="♀ (female)"]
  J14 = female pin header, 6 pins [form="♀ (female)"]
  J15 = female pin header, 6 pins [form="♀ (female)"]
  J16 = female pin header, 6 pins [form="♀ (female)"]
  LED3 = LED - 5mm [color="Green (570nm)" package="5 mm [THT]"]  # not connected
  LED4 = LED - 5mm [color="Red (633nm)" package="5 mm [THT]"]  # not connected
  J17 = female pin header, 4 pins [form="♀ (female)"]
  J18 = female pin header, 4 pins [form="♀ (female)"]
  J19 = female pin header, 4 pins [form="♀ (female)"]
  J20 = female pin header, 4 pins [form="♀ (female)"]
  J10 = female pin header, 2 pins [form="♀ (female)"]
  Part1 = Arduino ProtoShield

nets:
  N1: F1.2, Part1.N$162
  N2: F2.2, Part1.N$129
  GND: Part2.GND, J7.pin1, Part1.GND, Part1.N$64, Part1.N$176
  N3: J1.pin1, Part1.N$67
  N4: J1.pin2, Part1.N$56
  N5: J1.pin3, Part1.N$45
  N6: J1.pin4, Part1.N$34
  N7: J1.pin5, Part1.N$23
  N8: J1.pin6, Part1.N$12
  N9: J2.pin1, Part1.N$65
  N10: J2.pin2, Part1.N$54
  N11: J2.pin3, Part1.N$43
  N12: J2.pin4, Part1.N$32
  N13: J2.pin5, Part1.N$21
  N14: J2.pin6, Part1.N$10
  N15: J3.pin1, Part1.N$69
  N16: J3.pin2, Part1.N$58
  N17: J3.pin3, Part1.N$47
  N18: J3.pin4, Part1.N$36
  N19: J3.pin5, Part1.N$25
  N20: J3.pin6, Part1.N$14
  N21: J5.pin1, Part1.N$88
  N22: J5.pin2, Part1.N$87
  N23: J5.pin3, Part1.N$86
  N24: J6.pin1, Part1.N$99
  N25: J6.pin2, Part1.N$98
  N26: J6.pin3, Part1.N$97
  N27: J8.pin1, Part1.N$53
  N28: J8.pin2, Part1.N$42
  N29: J7.pin2, Part1.N$165
  N30: J7.pin3, Part1.N$154
  N31: J7.pin4, Part1.N$143
  N32: Part5.N$3, Part6.RX_LV
  N33: Part5.N$10, J14.pin6
  N34: Part5.N$12, J16.pin6
  N35: Part5.N$14, J15.pin6
  N36: Part5.N$15, Part6.RX_HV
  N37: Part5.N$18, Part6.LV
  N38: Part5.N$21, J14.pin5
  N39: Part5.N$23, J16.pin5
  N40: Part5.N$25, J15.pin5
  N41: Part5.N$26, Part6.HV
  N42: Part5.N$29, Part5.N$37, Part6.GND
  N43: Part5.N$32, J14.pin4
  N44: Part5.N$34, J16.pin4
  N45: Part5.N$36, J15.pin4
  N46: Part5.N$40, Part6.RX2_LV
  N47: Part5.N$42, J9.pin2
  N48: Part5.N$43, J14.pin3
  N49: Part5.N$45, J16.pin3
  N50: Part5.N$47, J15.pin3
  N51: Part5.N$48, Part6.RX2_HV
  N52: Part5.N$51, Part6.TX2_LV
  N53: Part5.N$53, J9.pin1
  N54: Part5.N$54, J14.pin2
  N55: Part5.N$56, J16.pin2
  N56: Part5.N$58, J15.pin2
  N57: Part5.N$59, Part6.TX2_HV
  N58: Part5.N$65, J14.pin1
  N59: Part5.N$67, J16.pin1
  N60: Part5.N$69, J15.pin1
  N61: Part5.N$86, J20.pin3
  N62: Part5.N$87, J20.pin2
  N63: Part5.N$88, J20.pin1
  N64: Part5.N$97, J19.pin3
  N65: Part5.N$98, J19.pin2
  N66: Part5.N$99, J19.pin1
  N67: Part5.N$108, J18.pin3
  N68: Part5.N$109, J18.pin2
  N69: Part5.N$110, J18.pin1
  N70: Part5.N$119, J17.pin3
  N71: Part5.N$120, J17.pin2
  N72: Part5.N$121, J17.pin1
  N73: Part5.N$129, F4.2
  N74: Part5.N$130, J13.pin3
  N75: Part5.N$131, J13.pin2
  N76: Part5.N$132, J13.pin1
  N77: Part5.N$141, J12.pin3
  N78: Part5.N$142, J12.pin2
  N79: Part5.N$143, J12.pin1
  N80: Part5.N$162, F3.2
  N81: Part5.N$165, J10.pin2
  N82: Part5.N$176, J10.pin1
  N83: Part1.RES, Part1.N$13, Part1.N$175
  N84: Part1.LED2, Part1.N$35
  N85: Part1.N$46, Part1.N$163
  N86: Part1.N$57, Part1.N$132
